# Fritzing sketch um-servo (saved by Fritzing 0.9.9b)

parts:
  Componente1 = 16-Channel 12-bit PWM Servo Driver - I2C [part_number=815]
  Componente2 = Arduino Uno (Rev3)
  J1 = Basic Servo
  JACK1 = 2.1mm Barrel Jack with Terminal Block

nets:
  N1: Componente1.PWRIN, JACK1.POS
  GND: Componente1.GND, Componente1.OE, Componente2.GND, J1.gnd, JACK1.NEG
  N2: Componente1.PWM0, J1.pulse
  N3: Componente1.5.0V, J1.vcc
  VCC: Componente1.VCC, Componente2.5V
  N4: Componente1.SDA, Componente2.A4/SDA
  N5: Componente1.SCL, Componente2.A5/SCL

custom parts:
  16-Channel 12-bit PWM Servo Driver - I2C: You want to make a cool robot, maybe a hexapod walker, or maybe just a piece of art with a lot of moving parts. Or maybe you want to drive a lot of LEDs with precise PWM output. Using only two pins, control 16 free-running PWM outputs! You can even chain up 62 breakouts to control up to 992 PWM outputs.
