# Fritzing sketch Untitled Sketch 2 (saved by Fritzing 0.9.9b)
breadboards: 1

parts:
  Componente1 = Arduino Uno (Rev3)
  LED1 = LED - 5mm [color="Red (633nm)" current=0.030 package="5 mm [THT]"]
  R1 = Resistor [tolerance=±5% power=0.25 resistance=220 package=THT]

nets:
  N1: Componente1.D8, R1.Pin_1
  N2: Componente1.GND, LED1.cathode
  N3: LED1.anode, R1.Pin_0
